// Logisim project Main bus.circ as structural Verilog: 1 circuit, main circuit Main bus
module Main_bus (
);

  Counter #(.width(16), .max('hffff)) Program_counter ();  // open: load, D, count, Q, carry, clk, clr
  Register Memory_access_register ();  // open: D, en, Q, clk, clr
  Register Instruction_register ();  // open: D, en, Q, clk, clr
  RAM ram_1 ();  // open: addr, data, sel, clk, ld, clr
  ROM rom_1 ();  // open: addr, data, sel
  Register Accumulator_register ();  // open: D, en, Q, clk, clr
  Register Input_register ();  // open: D, en, Q, clk, clr
  Register Output_register ();  // open: D, en, Q, clk, clr

  // Notes on the sheet:
  //   RAM for storage
  //   ROM for control matrix
  //   ALU
endmodule
